# Fritzing sketch diagram (saved by Fritzing 1.0.6)
breadboards: 1

parts:
  LED1 = LED - 5mm [color="Red (633nm)" current=0.030A package="5 mm [THT]"]
  S2 = Pushbutton [package="[SMD]"]
  T-Cobbler1 = T-Cobbler
  R1 = Resistor [tolerance=±5% resistance=220 package="2010 [SMD]"]

nets:
  N1: LED1.cathode, R1.Pin_1
  N2: LED1.anode, T-Cobbler1.GND#26
  N3: S2.Pin_1, S2.Pin_2, T-Cobbler1.GPIO26, R1.Pin_0
  N4: S2.Pin_3, S2.Pin_4, T-Cobbler1.GPIO23

custom parts:
  T-Cobbler: T-Cobbler for RPi B+ and Rpi2 from SunFounder
