# Fritzing sketch diagram (saved by Fritzing 1.0.6)
breadboards: 1

parts:
  LED1 = LED - 5mm [color="Red (633nm)" current=0.030A package="5 mm [THT]"]
  T-Cobbler1 = T-Cobbler
  HC-SR04_Sensor_1 = HC-SR04 Ultrasonic Distance Sensor
  R1 = Resistor [tolerance=±5% resistance=220 package="0603 [SMD]"]

nets:
  N1: LED1.cathode, T-Cobbler1.GND#34
  N2: LED1.anode, R1.Pin_1
  N3: T-Cobbler1.GPIO4, T-Cobbler1.ID_SD, T-Cobbler1.GPIO6, T-Cobbler1.GPIO19
  N4: T-Cobbler1.GPIO5, T-Cobbler1.GPIO13
  N5: T-Cobbler1.GND#26, HC-SR04_Sensor_1.TRIG
  N6: T-Cobbler1.GPIO23, HC-SR04_Sensor_1.ECHO
  N7: T-Cobbler1.ID_SC, HC-SR04_Sensor_1.GND
  N8: T-Cobbler1.GPIO12, R1.Pin_0

custom parts:
  T-Cobbler: T-Cobbler for RPi B+ and Rpi2 from SunFounder
